// Logisim project 2421 bcd to excess 3 pt2.circ as structural Verilog: 1 circuit, main circuit main
module main (
  input  A,
  input  B,
  input  C,
  input  D,
  output W,
  output X,
  output Y,
  output Z
);

  wire and_1_out, and_2_out, and_3_out, and_4_out, and_5_out, and_6_out, and_7_out, and_8_out, and_9_out,
       not_1_out, not_2_out, not_3_out, not_4_out;

  not not_1 (not_1_out, A);
  not not_2 (not_2_out, B);
  and and_1 (and_1_out, B, not_1_out);
  and and_2 (and_2_out, not_1_out, C);
  not not_3 (not_3_out, C);
  not not_4 (not_4_out, D);
  and and_3 (and_3_out, C, B, D);
  and and_4 (and_4_out, not_1_out, C, D);
  and and_5 (and_5_out, B, not_3_out, D);
  and and_6 (and_6_out, not_3_out, A);
  and and_7 (and_7_out, not_2_out, not_3_out, D);
  and and_8 (and_8_out, B, C, not_4_out);
  and and_9 (and_9_out, not_1_out, not_3_out, not_4_out);
  or or_1 (X, and_1_out, and_2_out, and_3_out, and_7_out);
  or or_2 (Y, and_8_out, and_4_out, and_5_out, and_9_out);
  or or_3 (Z, not_4_out, and_6_out);

  assign W = A;
endmodule
