// Logisim project 2421 bcd to excess 3.circ as structural Verilog: 1 circuit, main circuit main
module main (
  input  A,
  input  B,
  input  C,
  input  D,
  output W,
  output X,
  output Y,
  output Z
);

  wire and_1_out, and_2_out, and_3_out, and_4_out, and_6_out, and_7_out, and_8_out, and_9_out, and_10_out,
       and_11_out, and_12_out, and_13_out, and_14_out, and_15_out, not_1_out, not_2_out, not_3_out,
       not_4_out, not_5_out, not_6_out, not_7_out, or_1_out, or_2_out, or_3_out, or_4_out, xor_1_out;

  not not_1 (not_1_out, A);
  not not_2 (not_2_out, B);
  not not_3 (not_3_out, C);
  not not_4 (not_4_out, D);
  not not_5 (not_5_out, B);
  not not_6 (not_6_out, D);
  and and_1 (and_1_out, C, D);
  or or_1 (or_1_out, B, and_1_out);
  and and_2 (and_2_out, not_3_out, not_4_out);
  and and_3 (and_3_out, not_2_out, C, D);
  and and_4 (and_4_out, A, not_5_out, not_6_out);
  and and_5 (W, A, or_1_out);
  and and_6 (and_6_out, B, not_3_out, not_4_out);
  and and_7 (and_7_out, A, B);
  or or_2 (or_2_out, not_3_out, not_4_out);
  and and_8 (and_8_out, not_1_out, not_2_out);
  not not_7 (not_7_out, C);
  or or_3 (or_3_out, C, D);
  or or_4 (or_4_out, and_2_out, and_3_out);
  and and_9 (and_9_out, and_7_out, or_2_out);
  and and_10 (and_10_out, and_8_out, or_3_out);
  and and_11 (and_11_out, not_1_out, B, not_7_out, not_4_out);
  and and_12 (and_12_out, A, B, C, D);
  and and_13 (and_13_out, not_1_out, or_4_out);
  and and_14 (and_14_out, A, B);
  and and_15 (and_15_out, and_14_out, xor_1_out);
  xor xor_1 (xor_1_out, C, D);
  or or_5 (X, and_10_out, and_11_out, and_12_out);
  or or_6 (Z, and_6_out, and_4_out, and_9_out);
  or or_7 (Y, and_13_out, and_15_out);
endmodule
